// Logisim project registrador8bits.circ as structural Verilog: 7 circuits, main circuit main
module main (
  input  clk,
  input  enable,
  input  reset,
  input  a0,
  input  b0,
  input  a1,
  input  b1,
  input  a2,
  input  b2,
  input  a3,
  input  b3,
  input  a4,
  input  b4,
  input  a5,
  input  b5,
  input  a6,
  input  b6,
  input  a7,
  input  b7,
  output out_20,
  output out_21,
  output out_22,
  output out_23,
  output out_24,
  output out_25,
  output out_26,
  output out_27,
  output out_28,
  output out_29,
  output out_30,
  output out_31,
  output out_32,
  output out_33,
  output out_34,
  output out_35
);

  wire and_1_out, and_2_out, and_3_out, and_4_out, and_5_out, and_6_out, and_7_out, and_8_out, and_9_out,
       and_10_out, and_11_out, and_12_out, and_13_out, and_14_out, and_15_out, and_16_out, and_17_out,
       not_1_out;

  not not_1 (not_1_out, reset);
  and and_1 (and_1_out, not_1_out, a0);
  and and_2 (and_2_out, not_1_out, b0);
  and and_3 (and_3_out, not_1_out, a1);
  and and_4 (and_4_out, not_1_out, b1);
  and and_5 (and_5_out, not_1_out, a2);
  and and_6 (and_6_out, not_1_out, b2);
  and and_7 (and_7_out, not_1_out, a3);
  and and_8 (and_8_out, not_1_out, b3);
  and and_9 (and_9_out, not_1_out, a4);
  and and_10 (and_10_out, not_1_out, b4);
  and and_11 (and_11_out, not_1_out, a5);
  and and_12 (and_12_out, not_1_out, b5);
  and and_13 (and_13_out, not_1_out, a6);
  and and_14 (and_14_out, not_1_out, b6);
  and and_15 (and_15_out, not_1_out, a7);
  and and_16 (and_16_out, not_1_out, b7);
  and and_17 (and_17_out, clk, enable);
  registrador4bits registrador4bits1 (
    .in_1(and_17_out), .in_2(and_1_out), .in_3(and_2_out), .in_4(and_3_out), .in_5(and_4_out),
    .in_6(and_5_out), .in_7(and_6_out), .in_8(and_7_out), .in_9(and_8_out), .out_10(out_20), .out_11(out_21),
    .out_12(out_22), .out_13(out_23), .out_14(out_24), .out_15(out_25), .out_16(out_26), .out_17(out_27));
  registrador4bits registrador4bits2 (
    .in_1(and_17_out), .in_2(and_9_out), .in_3(and_10_out), .in_4(and_11_out), .in_5(and_12_out),
    .in_6(and_13_out), .in_7(and_14_out), .in_8(and_15_out), .in_9(and_16_out), .out_10(out_28),
    .out_11(out_29), .out_12(out_30), .out_13(out_31), .out_14(out_32), .out_15(out_33), .out_16(out_34),
    .out_17(out_35));
endmodule

module latchsr (
  input  r,
  input  s,
  output q
);

  wire not_2_out, or_1_out, or_2_out;

  or or_1 (or_1_out, r, not_2_out);
  or or_2 (or_2_out, q, s);
  not not_1 (q, or_1_out);
  not not_2 (not_2_out, or_2_out);
endmodule

module latchd (
  input  clk,
  input  d,
  output q
);

  wire and_1_out, and_2_out, not_1_out;

  not not_1 (not_1_out, d);
  and and_1 (and_1_out, clk, not_1_out);
  and and_2 (and_2_out, clk, d);
  latchsr latchsr_1 (.r(and_1_out), .s(and_2_out), .q(q));
endmodule

module flipflop (
  input  clk,
  input  d,
  output q
);

  wire latchd_1_q, not_1_out;

  not not_1 (not_1_out, clk);
  latchd latchd_1 (.clk(not_1_out), .d(d), .q(latchd_1_q));
  latchd latchd_2 (.clk(clk), .d(latchd_1_q), .q(q));
endmodule

module registrador1bits (
  input  clk,
  input  d0,
  input  d1,
  output out_4,
  output out_5
);

  flipflop flipflop_1 (.clk(clk), .d(d0), .q(out_4));
  flipflop flipflop_2 (.clk(clk), .d(d1), .q(out_5));
endmodule

module registrador2bits (
  input  clk,
  input  d0,
  input  d1,
  input  d2,
  input  d3,
  output q0,
  output q1,
  output q2,
  output q3
);

  registrador1bits registrador1bits_1 (.clk(clk), .d0(d0), .d1(d1), .out_4(q0), .out_5(q1));
  registrador1bits registrador1bits_2 (.clk(clk), .d0(d2), .d1(d3), .out_4(q2), .out_5(q3));
endmodule

module registrador4bits (
  input  in_1,
  input  in_2,
  input  in_3,
  input  in_4,
  input  in_5,
  input  in_6,
  input  in_7,
  input  in_8,
  input  in_9,
  output out_10,
  output out_11,
  output out_12,
  output out_13,
  output out_14,
  output out_15,
  output out_16,
  output out_17
);

  registrador2bits registrador2bits_1 (
    .clk(in_1), .d0(in_2), .d1(in_3), .d2(in_4), .d3(in_5), .q0(out_10), .q1(out_11), .q2(out_12), .q3(out_13));
  registrador2bits registrador2bits_2 (
    .clk(in_1), .d0(in_6), .d1(in_7), .d2(in_8), .d3(in_9), .q0(out_14), .q1(out_15), .q2(out_16), .q3(out_17));
endmodule
