// Logisim project somaregistra8bits.circ as structural Verilog: 5 circuits, main circuit main
module main (
  input  clk,
  input  enable,
  input  reset,
  input  sumsub,
  input  a0,
  input  b0,
  input  a1,
  input  b1,
  input  a2,
  input  b2,
  input  a3,
  input  b3,
  input  a0_2,
  input  b0_2,
  input  a1_2,
  input  enable_2,
  input  b1_2,
  input  reset_2,
  input  a2_2,
  input  b2_2,
  input  a3_2,
  input  b3_2,
  output out_23,
  output out_24,
  output out_25,
  output out_26,
  output out_27,
  output out_28,
  output out_29,
  output out_30,
  output out_31,
  output out_32,
  output out_33,
  output out_34,
  output out_35,
  output out_36,
  output out_37,
  output out_38,
  output out_39
);

  wire fulladder8bits_1_out_18, fulladder8bits_1_out_19, fulladder8bits_1_out_20, fulladder8bits_1_out_21,
       fulladder8bits_1_out_22, fulladder8bits_1_out_23, fulladder8bits_1_out_24, fulladder8bits_1_out_25;

  fulladder8bits fulladder8bits_1 (
    .sumsub(sumsub), .a0(a0), .b0(b0), .a0_2(a1), .b0_2(b1), .a0_3(a2), .b0_3(b2), .a0_4(a3), .b0_4(b3),
    .a0_5(a0_2), .b0_5(b0_2), .a0_6(a1_2), .b0_6(b1_2), .a0_7(a2_2), .b0_7(b2_2), .a0_8(a3_2), .b0_8(b3_2),
    .out_18(fulladder8bits_1_out_18), .out_19(fulladder8bits_1_out_19), .out_20(fulladder8bits_1_out_20),
    .out_21(fulladder8bits_1_out_21), .out_22(fulladder8bits_1_out_22), .out_23(fulladder8bits_1_out_23),
    .out_24(fulladder8bits_1_out_24), .out_25(fulladder8bits_1_out_25), .out_26(out_39));
  registrador8bits_main Registrador8bits (
    .clk(clk), .enable(enable), .reset(reset), .d0(fulladder8bits_1_out_18), .d0_2(fulladder8bits_1_out_19),
    .d0_3(fulladder8bits_1_out_20), .d0_4(fulladder8bits_1_out_21), .d0_5(fulladder8bits_1_out_22),
    .d0_6(fulladder8bits_1_out_23), .d0_7(fulladder8bits_1_out_24), .d0_8(fulladder8bits_1_out_25),
    .out_12(out_23), .out_13(out_24), .out_14(out_25), .out_15(out_26), .out_16(out_27), .out_17(out_28),
    .out_18(out_29), .out_19(out_30));
  registrador8bits_main Registrador8bits_2 (
    .clk(clk), .enable(enable_2), .reset(reset_2), .d0(fulladder8bits_1_out_18),
    .d0_2(fulladder8bits_1_out_19), .d0_3(fulladder8bits_1_out_20), .d0_4(fulladder8bits_1_out_21),
    .d0_5(fulladder8bits_1_out_22), .d0_6(fulladder8bits_1_out_23), .d0_7(fulladder8bits_1_out_24),
    .d0_8(fulladder8bits_1_out_25), .out_12(out_31), .out_13(out_32), .out_14(out_33), .out_15(out_34),
    .out_16(out_35), .out_17(out_36), .out_18(out_37), .out_19(out_38));
endmodule

module \xor  (
  input  in_1,
  input  in_2,
  output out_3
);

  wire and_1_out, and_2_out, not_1_out, not_2_out;

  not not_1 (not_1_out, in_1);
  not not_2 (not_2_out, in_2);
  and and_1 (and_1_out, not_1_out, in_2);
  and and_2 (and_2_out, in_1, not_2_out);
  or or_1 (out_3, and_1_out, and_2_out);
endmodule

module fulladder (
  input  ci,
  input  a,
  input  b,
  output So,
  output co
);

  wire and_1_out, and_2_out, xor_1_out_3;

  \xor  xor_1 (.in_1(a), .in_2(b), .out_3(xor_1_out_3));
  and and_1 (and_1_out, ci, xor_1_out_3);
  and and_2 (and_2_out, a, b);
  \xor  xor_2 (.in_1(ci), .in_2(xor_1_out_3), .out_3(So));
  or or_1 (co, and_1_out, and_2_out);
endmodule

module fulladder4bits (
  input  sumsub,
  input  a0,
  input  b0,
  input  a1,
  input  b1,
  input  a2,
  input  b2,
  input  a3,
  input  b3,
  output s1,
  output s2,
  output s3,
  output s4,
  output co
);

  wire fulladder_1_co, fulladder_2_co, fulladder_3_co, xor_1_out_3, xor_2_out_3, xor_3_out_3, xor_4_out_3;

  \xor  xor_1 (.in_1(b0), .in_2(sumsub), .out_3(xor_1_out_3));
  \xor  xor_2 (.in_1(b1), .in_2(sumsub), .out_3(xor_2_out_3));
  \xor  xor_3 (.in_1(b2), .in_2(sumsub), .out_3(xor_3_out_3));
  \xor  xor_4 (.in_1(b3), .in_2(sumsub), .out_3(xor_4_out_3));
  fulladder fulladder_1 (.ci(sumsub), .a(a0), .b(xor_1_out_3), .So(s1), .co(fulladder_1_co));
  fulladder fulladder_2 (.ci(fulladder_1_co), .a(a1), .b(xor_2_out_3), .So(s2), .co(fulladder_2_co));
  fulladder fulladder_3 (.ci(fulladder_2_co), .a(a2), .b(xor_3_out_3), .So(s3), .co(fulladder_3_co));
  fulladder fulladder_4 (.ci(fulladder_3_co), .a(a3), .b(xor_4_out_3), .So(s4), .co(co));
endmodule

module fulladder8bits (
  input  sumsub,
  input  a0,
  input  b0,
  input  a0_2,
  input  b0_2,
  input  a0_3,
  input  b0_3,
  input  a0_4,
  input  b0_4,
  input  a0_5,
  input  b0_5,
  input  a0_6,
  input  b0_6,
  input  a0_7,
  input  b0_7,
  input  a0_8,
  input  b0_8,
  output out_18,
  output out_19,
  output out_20,
  output out_21,
  output out_22,
  output out_23,
  output out_24,
  output out_25,
  output out_26
);

  wire fulladder4bits_1_co;

  fulladder4bits fulladder4bits_1 (
    .sumsub(sumsub), .a0(a0), .b0(b0), .a1(a0_2), .b1(b0_2), .a2(a0_3), .b2(b0_3), .a3(a0_4), .b3(b0_4),
    .s1(out_18), .s2(out_19), .s3(out_20), .s4(out_21), .co(fulladder4bits_1_co));
  fulladder4bits fulladder4bits_2 (
    .sumsub(fulladder4bits_1_co), .a0(a0_5), .b0(b0_5), .a1(a0_6), .b1(b0_6), .a2(a0_7), .b2(b0_7),
    .a3(a0_8), .b3(b0_8), .s1(out_22), .s2(out_23), .s3(out_24), .s4(out_25), .co(out_26));
endmodule
